# Fritzing sketch Circuit (saved by Fritzing 0.8.5b)
breadboards: 1

parts:
  Componente1 = Arduino Leonardo (Rev3b)
  R1 = Resistor [tolerance=±5% resistance=300 package=THT]
  R3 = Resistor [tolerance=±5% resistance=300 package=THT]
  LED1 = LED - 5mm [color="Green (555nm)" package="5 mm [THT]"]
  LED2 = LED - 5mm [color="Yellow (585nm)" package="5 mm [THT]"]
  LED3 = LED - 5mm [color="Red (633nm)" package="5 mm [THT]"]
  R4 = Resistor [tolerance=±5% resistance=300 package=THT]
  R5 = Photocell (LDR) [package=THT]
  R6 = Resistor [tolerance=±5% resistance=10k package=THT]

nets:
  N1: Componente1.5V, R5.pin_1
  N2: Componente1.GND, LED1.cathode, LED2.cathode, LED3.cathode, R6.Pin_0
  N3: Componente1.A0, R5.pin_0, R6.Pin_1
  N4: Componente1.D8/A8, R1.Pin_0
  N5: Componente1.D9_PWM/A9, R4.Pin_0
  N6: Componente1.D10_PWM/A10, R3.Pin_0
  N7: R1.Pin_1, LED1.anode
  N8: R3.Pin_1, LED3.anode
  N9: LED2.anode, R4.Pin_1
