# Fritzing sketch Datasheet (saved by Fritzing 0.8.5b)
breadboards: 1

parts:
  LCD1 = LCD screen
  LED1 = LED - 5mm [color="Red (633nm)" package="5 mm [THT]"]
  LED2 = LED - 5mm [color="Yellow (595nm)" package="5 mm [THT]"]
  LED3 = LED - 5mm [color="Green (560nm)" package="5 mm [THT]"]
  R1 = Resistor [tolerance=±5% resistance=300 package=THT]
  R2 = Resistor [tolerance=±5% resistance=300 package=THT]
  R3 = Resistor [tolerance=±5% resistance=300 package=THT]
  R5 = Photocell (LDR) [package=THT]
  R6 = Resistor [tolerance=±5% resistance=10k package=THT]
  Componente1 = Arduino Uno (Rev3)
  R4 = Rotary Potentiometer (Large) [package=THT]

nets:
  VSS: LCD1.VSS, LCD1.R/W, LED1.cathode, LED2.cathode, LED3.cathode, R6.Pin_0, Componente1.GND, R4.leg2
  VDD: LCD1.VDD, R5.pin_1, Componente1.5V, R4.leg1
  N1: LCD1.V0, R4.wiper
  N2: LCD1.RS, Componente1.D2
  N3: LCD1.E, Componente1.D3_PWM
  N4: LCD1.DB4, Componente1.D4
  N5: LCD1.DB5, Componente1.D5_PWM
  N6: LCD1.DB6, Componente1.D6_PWM
  N7: LCD1.DB7, Componente1.D7
  N8: LED1.anode, R1.Pin_1
  N9: LED2.anode, R2.Pin_1
  N10: LED3.anode, R3.Pin_1
  N11: R1.Pin_0, Componente1.D8
  N12: R2.Pin_0, R3.Pin_0, Componente1.D9_PWM
  N13: R5.pin_0, R6.Pin_1, Componente1.A0
